# Fritzing sketch clock sparkcore (saved by Fritzing 0.9.0b)
circuit board: 8.46667cm x 5.64444cm
breadboards: 1

parts:
  8x8_LED_Matrix1 = 8x8 LED Matrix 1388ASR
  U1 = MAX7219 [package=dil24]
  8x8_LED_Matrix2 = 8x8 LED Matrix 1388ASR
  U2 = MAX7219 [package=dil24]
  8x8_LED_Matrix3 = 8x8 LED Matrix 1388ASR
  8x8_LED_Matrix4 = 8x8 LED Matrix 1388ASR
  U3 = MAX7219 [package=dil24]
  U4 = MAX7219 [package=dil24]
  8x8_LED_Matrix5 = 8x8 LED Matrix 1388ASR
  8x8_LED_Matrix6 = 8x8 LED Matrix 1388ASR
  U5 = MAX7219 [package=dil24]
  U6 = MAX7219 [package=dil24]
  元件1 = Spark Core (v1.0)
  LED1 = LEDs [package=led10mm]  # not connected
  JP1 = Jumper [package=sj_2s-no]  # not connected
  F1 = FUSE [package=fuse_5mm]
  C1 = Electrolytic Capacitor [capacitance=1000μF package="1010 [SMD, electrolytic]"]
  C2 = Ceramic Capacitor [capacitance=0.1mF package="0603 [SMD, multilayer]"]
  C3 = Electrolytic Capacitor [capacitance=1000μF package="1010 [SMD, electrolytic]"]
  C4 = Ceramic Capacitor [capacitance=0.1mF package="0603 [SMD, multilayer]"]
  C5 = Electrolytic Capacitor [capacitance=1000μF package="1010 [SMD, electrolytic]"]
  C6 = Ceramic Capacitor [capacitance=0.1mF package="0603 [SMD, multilayer]"]
  C7 = Electrolytic Capacitor [capacitance=1000μF package="1010 [SMD, electrolytic]"]
  C8 = Ceramic Capacitor [capacitance=0.1mF package="0603 [SMD, multilayer]"]
  C9 = Electrolytic Capacitor [capacitance=1000μF package="1010 [SMD, electrolytic]"]
  C10 = Ceramic Capacitor [capacitance=0.1mF package="0603 [SMD, multilayer]"]
  C11 = Electrolytic Capacitor [capacitance=1000μF package="1010 [SMD, electrolytic]"]
  C12 = Ceramic Capacitor [capacitance=0.1mF package="0603 [SMD, multilayer]"]
  R1 = Resistor [tolerance=±5% resistance=10k package=THT]
  R2 = Resistor [tolerance=±5% resistance=10k package=THT]
  R3 = Resistor [tolerance=±5% resistance=10k package=THT]
  R4 = Resistor [tolerance=±5% resistance=10k package=THT]
  R5 = Resistor [tolerance=±5% resistance=10k package=THT]
  R6 = Resistor [tolerance=±5% resistance=10k package=THT]
  LCD1 = LCD screen

nets:
  N1: 8x8_LED_Matrix1.Pin_1, U1.SEGD
  N2: 8x8_LED_Matrix1.Pin_2, U1.SEGF
  N3: 8x8_LED_Matrix1.Pin_3, U1.DIG1
  N4: 8x8_LED_Matrix1.Pin_4, U1.DIG2
  N5: 8x8_LED_Matrix1.Pin_5, U1.SEGG
  N6: 8x8_LED_Matrix1.Pin_6, U1.DIG4
  N7: 8x8_LED_Matrix1.Pin_7#7, U1.SEGE
  N8: 8x8_LED_Matrix1.Pin_8, U1.SEGB
  N9: 8x8_LED_Matrix1.Pin_9, U1.SEGDP
  N10: 8x8_LED_Matrix1.Pin_7#10, U1.DIG3
  N11: 8x8_LED_Matrix1.Pin_11, U1.DIG5
  N12: 8x8_LED_Matrix1.Pin_12, U1.SEGC
  N13: 8x8_LED_Matrix1.Pin_13, U1.DIG0
  N14: 8x8_LED_Matrix1.Pin14, U1.SEGA
  N15: 8x8_LED_Matrix1.Pin_15, U1.DIG6
  N16: 8x8_LED_Matrix1.Pin_16, U1.DIG7
  N17: U1.DIN, 元件1.A0
  N18: U1.GND, C1.-, C2.0
  GND2: U1.GND2, U2.GND2, U3.GND2, U4.GND2, U5.GND, U5.GND2, U6.GND, U6.GND2, 元件1.GND, C9.-, C10.0, C11.-, C12.0
  N19: U1.LOAD, U2.LOAD, U3.LOAD, U4.LOAD, U5.LOAD, U6.LOAD, 元件1.A1
  N20: U1.CLK, U2.CLK, U3.CLK, U4.CLK, U5.CLK, U6.CLK, 元件1.A2
  N21: U1.ISET, R2.Pin_1
  VCC: U1.VCC, U2.VCC, U3.VCC, U4.VCC, U5.VCC, U6.VCC, 元件1.VIN, F1.1, C1.+, C2.1, C3.+, C4.1, C5.+, C6.1, C7.+, C8.1, C9.+, C10.1, C11.+, C12.1, R1.Pin_0, R2.Pin_0, R3.Pin_0, R4.Pin_0, R5.Pin_0, R6.Pin_0, LCD1.VCC
  N22: U1.DOUT, U2.DIN
  N23: 8x8_LED_Matrix2.Pin_1, U2.SEGD
  N24: 8x8_LED_Matrix2.Pin_2, U2.SEGF
  N25: 8x8_LED_Matrix2.Pin_3, U2.DIG1
  N26: 8x8_LED_Matrix2.Pin_4, U2.DIG2
  N27: 8x8_LED_Matrix2.Pin_5, U2.SEGG
  N28: 8x8_LED_Matrix2.Pin_6, U2.DIG4
  N29: 8x8_LED_Matrix2.Pin_7#7, U2.SEGE
  N30: 8x8_LED_Matrix2.Pin_8, U2.SEGB
  N31: 8x8_LED_Matrix2.Pin_9, U2.SEGDP
  N32: 8x8_LED_Matrix2.Pin_7#10, U2.DIG3
  N33: 8x8_LED_Matrix2.Pin_11, U2.DIG5
  N34: 8x8_LED_Matrix2.Pin_12, U2.SEGC
  N35: 8x8_LED_Matrix2.Pin_13, U2.DIG0
  N36: 8x8_LED_Matrix2.Pin14, U2.SEGA
  N37: 8x8_LED_Matrix2.Pin_15, U2.DIG6
  N38: 8x8_LED_Matrix2.Pin_16, U2.DIG7
  N39: U2.GND, C3.-, C4.0
  N40: U2.ISET, R1.Pin_1
  N41: U2.DOUT, U3.DIN
  N42: 8x8_LED_Matrix3.Pin_1, U4.SEGD
  N43: 8x8_LED_Matrix3.Pin_2, U4.SEGF
  N44: 8x8_LED_Matrix3.Pin_3, U4.DIG1
  N45: 8x8_LED_Matrix3.Pin_4, U4.DIG2
  N46: 8x8_LED_Matrix3.Pin_5, U4.SEGG
  N47: 8x8_LED_Matrix3.Pin_6, U4.DIG4
  N48: 8x8_LED_Matrix3.Pin_7#7, U4.SEGE
  N49: 8x8_LED_Matrix3.Pin_8, U4.SEGB
  N50: 8x8_LED_Matrix3.Pin_9, U4.SEGDP
  N51: 8x8_LED_Matrix3.Pin_7#10, U4.DIG3
  N52: 8x8_LED_Matrix3.Pin_11, U4.DIG5
  N53: 8x8_LED_Matrix3.Pin_12, U4.SEGC
  N54: 8x8_LED_Matrix3.Pin_13, U4.DIG0
  N55: 8x8_LED_Matrix3.Pin14, U4.SEGA
  N56: 8x8_LED_Matrix3.Pin_15, U4.DIG6
  N57: 8x8_LED_Matrix3.Pin_16, U4.DIG7
  N58: 8x8_LED_Matrix4.Pin_1, U3.SEGD
  N59: 8x8_LED_Matrix4.Pin_2, U3.SEGF
  N60: 8x8_LED_Matrix4.Pin_3, U3.DIG1
  N61: 8x8_LED_Matrix4.Pin_4, U3.DIG2
  N62: 8x8_LED_Matrix4.Pin_5, U3.SEGG
  N63: 8x8_LED_Matrix4.Pin_6, U3.DIG4
  N64: 8x8_LED_Matrix4.Pin_7#7, U3.SEGE
  N65: 8x8_LED_Matrix4.Pin_8, U3.SEGB
  N66: 8x8_LED_Matrix4.Pin_9, U3.SEGDP
  N67: 8x8_LED_Matrix4.Pin_7#10, U3.DIG3
  N68: 8x8_LED_Matrix4.Pin_11, U3.DIG5
  N69: 8x8_LED_Matrix4.Pin_12, U3.SEGC
  N70: 8x8_LED_Matrix4.Pin_13, U3.DIG0
  N71: 8x8_LED_Matrix4.Pin14, U3.SEGA
  N72: 8x8_LED_Matrix4.Pin_15, U3.DIG6
  N73: 8x8_LED_Matrix4.Pin_16, U3.DIG7
  N74: U3.GND, C5.-, C6.0
  N75: U3.ISET, R3.Pin_1
  N76: U3.DOUT, U4.DIN
  N77: U4.ISET, R4.Pin_1
  N78: U4.DOUT, U5.DIN
  N79: 8x8_LED_Matrix5.Pin_1, U6.SEGD
  N80: 8x8_LED_Matrix5.Pin_2, U6.SEGF
  N81: 8x8_LED_Matrix5.Pin_3, U6.DIG1
  N82: 8x8_LED_Matrix5.Pin_4, U6.DIG2
  N83: 8x8_LED_Matrix5.Pin_5, U6.SEGG
  N84: 8x8_LED_Matrix5.Pin_6, U6.DIG4
  N85: 8x8_LED_Matrix5.Pin_7#7, U6.SEGE
  N86: 8x8_LED_Matrix5.Pin_8, U6.SEGB
  N87: 8x8_LED_Matrix5.Pin_9, U6.SEGDP
  N88: 8x8_LED_Matrix5.Pin_7#10, U6.DIG3
  N89: 8x8_LED_Matrix5.Pin_11, U6.DIG5
  N90: 8x8_LED_Matrix5.Pin_12, U6.SEGC
  N91: 8x8_LED_Matrix5.Pin_13, U6.DIG0
  N92: 8x8_LED_Matrix5.Pin14, U6.SEGA
  N93: 8x8_LED_Matrix5.Pin_15, U6.DIG6
  N94: 8x8_LED_Matrix5.Pin_16, U6.DIG7
  N95: 8x8_LED_Matrix6.Pin_1, U5.SEGD
  N96: 8x8_LED_Matrix6.Pin_2, U5.SEGF
  N97: 8x8_LED_Matrix6.Pin_3, U5.DIG1
  N98: 8x8_LED_Matrix6.Pin_4, U5.DIG2
  N99: 8x8_LED_Matrix6.Pin_5, U5.SEGG
  N100: 8x8_LED_Matrix6.Pin_6, U5.DIG4
  N101: 8x8_LED_Matrix6.Pin_7#7, U5.SEGE
  N102: 8x8_LED_Matrix6.Pin_8, U5.SEGB
  N103: 8x8_LED_Matrix6.Pin_9, U5.SEGDP
  N104: 8x8_LED_Matrix6.Pin_7#10, U5.DIG3
  N105: 8x8_LED_Matrix6.Pin_11, U5.DIG5
  N106: 8x8_LED_Matrix6.Pin_12, U5.SEGC
  N107: 8x8_LED_Matrix6.Pin_13, U5.DIG0
  N108: 8x8_LED_Matrix6.Pin14, U5.SEGA
  N109: 8x8_LED_Matrix6.Pin_15, U5.DIG6
  N110: 8x8_LED_Matrix6.Pin_16, U5.DIG7
  N111: U5.ISET, R5.Pin_1
  N112: U5.DOUT, U6.DIN
  N113: U6.ISET, R6.Pin_1
  N114: 元件1.D1, LCD1.SCL
  N115: C7.-, C8.0

custom parts:
  8x8 LED Matrix 1388ASR: Red Color Common Anode 8x8 LED Matrix
  LCD screen: A standard character display, usually with 2x16 characters. Comes in many colors.
